// Logisim project Lab-2.circ as structural Verilog: 1 circuit, main circuit main
module main (
  input  [7:0] in_1,
  input  [1:0] in_2,
  input  [7:0] in_3,
  input  [1:0] in_4,
  input  [7:0] in_5,
  input  in_6,
  input  [7:0] in_7,
  input  [2:0] in_8,
  input  [1:0] in_9,
  input  [7:0] in_10,
  input  in_11,
  input  [7:0] in_12,
  output [7:0] out_13,
  output [7:0] out_14,
  output [7:0] out_15,
  output [7:0] out_16
);

  wire clock_1_out, clock_2_out, clock_3_out, decoder_1_out0, decoder_1_out1, decoder_1_out2, decoder_1_out3,
       decoder_2_out0, decoder_2_out1, decoder_2_out2, decoder_2_out3;
  wire [1:0] not_2_out;
  wire [7:0] adder_1_out, adder_2_out, adder_3_out, and_1_out, and_2_out, nand_1_out, not_1_out, or_1_out,
       register_1_q, register_2_q, register_3_q, register_4_q, register_5_q, register_6_q, register_7_q,
       register_8_q, subtractor_1_out, subtractor_2_out, subtractor_3_out, xor_1_out;

  Clock clock_1 (.out(clock_1_out));
  Adder adder_1 (.a(in_3), .b(in_5), .out(adder_1_out));  // open: cin, cout
  Subtractor subtractor_1 (.a(in_3), .b(in_5), .out(subtractor_1_out));  // open: bin, bout
  assign and_1_out = in_3 & in_5;  // AND_Gate and_1, 8 bits wide
  assign nand_1_out = ~(in_3 & in_5);  // NAND_Gate nand_1, 8 bits wide
  Adder adder_2 (.a(in_10), .b(8'h1), .out(adder_2_out));  // open: cin, cout
  Subtractor subtractor_2 (.a(in_10), .b(8'h1), .out(subtractor_2_out));  // open: bin, bout
  Adder adder_3 (.a(in_10), .b(in_12), .out(adder_3_out));  // open: cin, cout
  Subtractor subtractor_3 (.a(in_10), .b(in_12), .out(subtractor_3_out));  // open: bin, bout
  assign and_2_out = in_10 & in_12;  // AND_Gate and_2, 8 bits wide
  assign or_1_out = in_10 | in_12;  // OR_Gate or_1, 8 bits wide
  assign not_1_out = ~in_10;  // NOT_Gate not_1, 8 bits wide
  assign xor_1_out = in_10 ^ in_12;  // XOR_Gate xor_1, 8 bits wide
  Multiplexer #(.select(2), .width(8)) multiplexer_1 (
    .in0(adder_1_out), .in1(subtractor_1_out), .in2(and_1_out), .in3(nand_1_out), .out(out_13), .sel(in_2),
    .en(clock_1_out));
  Clock clock_2 (.out(clock_2_out));
  Multiplexer #(.select(3), .width(8), .enable("false")) multiplexer_2 (
    .in0(adder_2_out), .in1(subtractor_2_out), .in2(adder_3_out), .in3(subtractor_3_out), .in4(and_2_out),
    .in5(or_1_out), .in6(not_1_out), .in7(xor_1_out), .out(out_15), .sel(in_8));
  Decoder #(.select(2)) decoder_1 (
    .out0(decoder_1_out0), .out1(decoder_1_out1), .out2(decoder_1_out2), .out3(decoder_1_out3), .sel(in_4),
    .en(in_6));
  Register register_1 (.D(in_1), .en(decoder_1_out0), .Q(register_1_q), .clk(clock_2_out));  // open: clr
  Register register_2 (.D(in_1), .en(decoder_1_out1), .Q(register_2_q), .clk(clock_2_out));  // open: clr
  Register register_3 (.D(in_1), .en(decoder_1_out2), .Q(register_3_q), .clk(clock_2_out));  // open: clr
  Register register_4 (.D(in_1), .en(decoder_1_out3), .Q(register_4_q), .clk(clock_2_out));  // open: clr
  Clock clock_3 (.out(clock_3_out));
  Multiplexer #(.select(2), .width(8), .enable("false")) multiplexer_3 (
    .in0(register_1_q), .in1(register_2_q), .out(out_14), .sel(in_4));  // open: in2, in3
  Decoder #(.select(2)) decoder_2 (
    .out0(decoder_2_out0), .out1(decoder_2_out1), .out2(decoder_2_out2), .out3(decoder_2_out3), .sel(in_9),
    .en(in_11));
  assign not_2_out = ~in_9;  // NOT_Gate not_2, 2 bits wide
  Register register_5 (.D(in_7), .en(decoder_2_out0), .Q(register_5_q), .clk(clock_3_out));  // open: clr
  Register register_6 (.D(in_7), .en(decoder_2_out1), .Q(register_6_q), .clk(clock_3_out));  // open: clr
  Register register_7 (.D(in_7), .en(decoder_2_out2), .Q(register_7_q), .clk(clock_3_out));  // open: clr
  Register register_8 (.D(in_7), .en(decoder_2_out3), .Q(register_8_q), .clk(clock_3_out));  // open: clr
  Multiplexer #(.select(2), .width(8), .enable("false")) multiplexer_4 (
    .in0(register_5_q), .in1(register_6_q), .in2(register_7_q), .in3(register_8_q), .out(out_16),
    .sel(not_2_out));
endmodule
